// Logisim project TallerLogica-Combinatorios.circ as structural Verilog: 9 circuits, main circuit sumSimp
module sumSimp (
  input  A,
  input  B,
  output S,
  output Cout
);

  xor xor_1 (S, A, B);
  and and_1 (Cout, A, B);
endmodule

module sumComp (
  input  Cin,
  input  a,
  input  b,
  output S,
  output Cout
);

  wire sumsimp_1_cout, sumsimp_1_s, sumsimp_2_cout;

  sumSimp sumsimp_1 (.A(a), .B(b), .S(sumsimp_1_s), .Cout(sumsimp_1_cout));
  sumSimp sumsimp_2 (.A(Cin), .B(sumsimp_1_s), .S(S), .Cout(sumsimp_2_cout));
  xor xor_1 (Cout, sumsimp_2_cout, sumsimp_1_cout);
endmodule

module sum4b (
  input  [3:0] a,
  input  [3:0] b,
  output [3:0] S,
  output Cout
);

  wire sumcomp_1_cout, sumcomp_2_cout, sumcomp_3_cout;

  sumComp sumcomp_1 (.Cin(1'b0), .a(a[0]), .b(b[0]), .S(S[0]), .Cout(sumcomp_1_cout));
  sumComp sumcomp_2 (.Cin(sumcomp_3_cout), .a(a[2]), .b(b[2]), .S(S[2]), .Cout(sumcomp_2_cout));
  sumComp sumcomp_3 (.Cin(sumcomp_1_cout), .a(a[1]), .b(b[1]), .S(S[1]), .Cout(sumcomp_3_cout));
  sumComp sumcomp_4 (.Cin(sumcomp_2_cout), .a(a[3]), .b(b[3]), .S(S[3]), .Cout(Cout));
endmodule

module Comp (
  input  [3:0] in_1,
  output out_2
);

  wire and_1_out, and_2_out, not_1_out, not_2_out, not_3_out, not_4_out;

  not not_1 (not_1_out, in_1[0]);
  not not_2 (not_2_out, in_1[1]);
  not not_3 (not_3_out, in_1[2]);
  not not_4 (not_4_out, in_1[3]);
  and and_1 (and_1_out, not_1_out, not_2_out);
  and and_2 (and_2_out, not_3_out, not_4_out);
  and and_3 (out_2, and_1_out, and_2_out);
endmodule

module ZCVN (
  input  [3:0] A,
  input  [3:0] B,
  output V,
  output N,
  output [3:0] S,
  output Z,
  output C
);

  wire and_1_out, and_2_out, and_3_out, not_1_out, not_2_out, xor_1_out;

  and and_1 (and_1_out, B[3], A[3]);
  not not_1 (not_1_out, B[3]);
  not not_2 (not_2_out, A[3]);
  and and_2 (and_2_out, not_1_out, not_2_out);
  xor xor_1 (xor_1_out, and_1_out, N);
  and and_3 (and_3_out, and_2_out, N);
  sum4b sum4b_1 (.a(A), .b(B), .S({N, S[2:0]}), .Cout(C));
  or or_1 (V, xor_1_out, and_3_out);
  Comp comp_1 (.in_1({N, S[2:0]}), .out_2(Z));

  assign S[3] = N;
endmodule

module incr4b (
  input  [3:0] A,
  output [3:0] out_2
);

  sum4b sum4b_1 (.a(A), .b(4'b0001), .S(out_2));  // open: Cout
endmodule

module InvC (
  input  [3:0] in_1,
  input  [3:0] in_2,
  input  in_3,
  input  in_4,
  output [3:0] out_5,
  output [3:0] out_6
);

  wire [3:0] incr4b_1_out_2, not_1_out;

  assign not_1_out = ~in_1;  // NOT_Gate not_1, 4 bits wide
  // NOT_Gate not_2 is placed but not wired
  incr4b incr4b_1 (.A(not_1_out), .out_2(incr4b_1_out_2));
  incr4b incr4b_2 ();  // open: A, out_2
  Multiplexer #(.width(4)) multiplexer_1 (.in0(in_1), .in1(incr4b_1_out_2), .out(out_5), .sel(in_3));
  // Multiplexer #(.width(4)) multiplexer_2: pin names not known; wires that end beside it: in_3, out_6

  assign in_2 = in_1;
endmodule

module inversor_4 (
  input  [3:0] a,
  input  inv,
  output [3:0] out_3
);

  xor xor_1 (out_3[0], a[0], inv);
  xor xor_2 (out_3[1], a[1], inv);
  xor xor_3 (out_3[2], a[2], inv);
  xor xor_4 (out_3[3], a[3], inv);
endmodule

module ALU (
  input  [3:0] A,
  input  [3:0] B,
  input  [1:0] OP,
  output V,
  output C,
  output N,
  output [3:0] S,
  output Z
);

  wire not_1_out, zcvn_1_c, zcvn_1_v, zcvn_2_c, zcvn_2_v;
  wire [3:0] and_1_out, invc_1_out_5, or_1_out, zcvn_1_s, zcvn_2_s;

  InvC invc_1 (.in_1(B), .in_2(B), .in_3(1'b1), .in_4(1'b1), .out_5(invc_1_out_5));  // open: out_6
  ZCVN zcvn_1 (.A(A), .B(B), .V(zcvn_1_v), .S(zcvn_1_s), .C(zcvn_1_c));  // open: N, Z
  ZCVN zcvn_2 (.A(A), .B(invc_1_out_5), .V(zcvn_2_v), .S(zcvn_2_s), .C(zcvn_2_c));  // open: N, Z
  assign and_1_out = A & B;  // AND_Gate and_1, 4 bits wide
  assign or_1_out = A | B;  // OR_Gate or_1, 4 bits wide
  not not_1 (not_1_out, zcvn_2_c);
  Multiplexer #(.select(2), .width(4)) multiplexer_1 (
    .in0(zcvn_1_s), .in1(zcvn_2_s), .in2(and_1_out), .in3(or_1_out), .out({N, S[2:0]}), .sel(OP));
  Multiplexer #(.select(2)) multiplexer_2 (.in0(zcvn_1_v), .in1(zcvn_2_v), .in2(1'b0), .in3(1'b0), .out(V), .sel(OP));
  Multiplexer #(.select(2)) multiplexer_3 (.in0(zcvn_1_c), .in1(not_1_out), .in2(1'b0), .in3(1'b0), .out(C), .sel(OP));
  Comp comp_1 (.in_1({N, S[2:0]}), .out_2(Z));

  assign S[3] = N;
endmodule
